# Fritzing sketch BTS7960 interface 4 (saved by Fritzing 0.9.3b)
circuit board: 2.6cm x 1.9043cm
breadboards: 1

parts:
  J1 = female pin header, 4 pins [form="♀ (female)"]
  7 = female pin header, 1 pin [form="♀ (female)"]
  8 = female pin header, 1 pin [form="♀ (female)"]
  6 = female pin header, 1 pin [form="♀ (female)"]
  5 = female pin header, 1 pin [form="♀ (female)"]
  1 = female pin header, 1 pin [form="♀ (female)"]
  2 = female pin header, 1 pin [form="♀ (female)"]
  4 = female pin header, 1 pin [form="♀ (female)"]
  3 = female pin header, 1 pin [form="♀ (female)"]
  R1-1K = Resistor [tolerance=±5% resistance=1k package=THT]
  R2-1K = Resistor [tolerance=±5% resistance=1k package=THT]
  LED = LED - 5mm [color="Green (565nm)" package="5 mm [THT]"]
  R3-470 = Resistor [tolerance=±5% resistance=470 package=THT]
  2N2222 = PNP-Transistor [package="TO92 [THT]"]

nets:
  N1: J1.pin1, 1.pin1, R2-1K.Pin_1
  N2: J1.pin2, 7.pin1, 4.pin1, 3.pin1, R1-1K.Pin_1, R3-470.Pin_1
  N3: J1.pin3, 6.pin1, 5.pin1
  N4: J1.pin4, 8.pin1, LED.anode, 2N2222.E
  N5: 2.pin1, R1-1K.Pin_0, 2N2222.C
  N6: R2-1K.Pin_0, 2N2222.B
  N7: LED.cathode, R3-470.Pin_0

notes:
  BTS7960 plug v1
  Bob Gamble
  GND  SEN  EN  DCC
  E
  B
  C
