# Fritzing sketch DCC Nano 2c (saved by Fritzing 0.9.3b)
circuit board: 7.2cm x 3.31069cm
breadboards: 1

parts:
  J1 = Camdenboss CTB0158-2 [part_number=CTB0158-2 package=THT]
  6N137 = IC, DIP package, 8 pins [chip_label=6N137 part_number=6N137]
  10K = Resistor [tolerance=±5% resistance=10k package=THT]
  1N4148 = Rectifier Diode [part_number=1N4148 package="300 mil [THT]"]
  1K = Resistor [tolerance=±5% resistance=1k package=THT]
  10K_2 = Resistor [tolerance=±5% resistance=10k package=THT]
  Power_In = Power plug
  J2 = Camdenboss CTB0158-2 [part_number=CTB0158-2 package=THT]
  Arduino_Nano = Arduino Nano (Rev3.0)

nets:
  N1: J1.pin1, 6N137.pin3, 1N4148.anode
  N2: J1.pin2, 1K.Pin_0
  N3: 6N137.pin2, 1N4148.cathode, 1K.Pin_1
  GND: 6N137.pin5, Power_In.GND, J2.pin1, Arduino_Nano.GND
  N4: 6N137.pin6, 10K.Pin_1, Arduino_Nano.D2
  N5: 6N137.pin7, 10K_2.Pin_1
  VCC: 6N137.pin8, 10K.Pin_0, 10K_2.Pin_0, Power_In.VCC, J2.pin2, Arduino_Nano.5V

notes:
  to DCC
  5V DC
  DCC Interface - http://www.mynabay.com/dcc_monitor/
  Bob Gamble
  DCC IN
  TX1 RX0 RST GND D2  D3 D4  D5  D6  D7  D8  D9 D10 D11 D12
  D13 3V3 REF A0  A1  A2  A3  A4  A5  A6 A7 5V RST GND VIN
  <- GRND
  Rev 1.1c
  GRND->
  7-12v   5v
  Input
  Jumper
  D12 D11 D10 D9  D8  D7  D6  D5  D4 D3  D2 GND RST RX0 TX1
  VIN GND RST  5V A7  A6 A5  A4  A3  A2  A1  A0 REF 3V3 D13
