# Fritzing sketch DCC Nano 2g (saved by Fritzing 0.9.3b)
circuit board: 6.7cm x 3.3cm
breadboards: 1

parts:
  6N137 = IC, DIP package, 8 pins [chip_label=6N137 part_number=6N137]
  5K = Resistor [tolerance=±5% resistance=4.7k package=THT]
  1N4148 = Rectifier Diode [part_number=1N4148 package="300 mil [THT]"]
  1_3K = Resistor [tolerance=±5% resistance=1.5k package=THT]
  10K = Resistor [tolerance=±5% resistance=10k package=THT]
  +_Power_In_- = Power plug
  J1 = Screw terminal - 2 pins [package=THT]
  J2 = screw terminal, 2 pins
  270pF = Ceramic Capacitor [capacitance=0.1nF package="200 mil [THT, multilayer]"]
  Arduino_Nano = Arduino Nano (Rev3.0)

nets:
  N1: 6N137.pin2, 1N4148.cathode, 1_3K.Pin_1, 270pF.0
  N2: 6N137.pin3, 1N4148.anode, J1.pin1, 270pF.1
  GND: 6N137.pin5, +_Power_In_-.GND, J2.pin2, Arduino_Nano.GND
  N3: 6N137.pin6, 5K.Pin_1, Arduino_Nano.D2
  N4: 6N137.pin7, 10K.Pin_1
  VCC: 6N137.pin8, 5K.Pin_0, 10K.Pin_0, +_Power_In_-.VCC, J2.pin1, Arduino_Nano.5V
  N5: 1_3K.Pin_0, J1.pin2

notes:
  to DCC
  5V DC
  DCC Interface - http://www.mynabay.com/dcc_monitor/
  Bob Gamble
  DCC IN
  D1/TX D0/RX RST GND  D2  D3*  D4  D5*  D6* D7  D8   D9* D10* D11* D12
  D13 3V3 REF A0  A1  A2  A3  A4  A5  A6 A7 5V RST GND VIN
  <- GRND
  Rev 1.3
  7-12v   5v
  Input
  Jumper
  D12 D11* D10* D9*  D8  D7  D6*  D5*  D4 D3*  D2  GND RST D0/RX D1/TX
  VIN GND RST  5V A7  A6 A5  A4  A3  A2  A1  A0 REF 3V3 D13
  DCC Nano Interface
  +       -
