# Fritzing sketch DCC Nano 3b (saved by Fritzing 0.9.3b)
circuit board: 6.35611cm x 3.49555cm
breadboards: 1

parts:
  6N137 = IC, DIP package, 8 pins [chip_label=6N137 part_number=6N137]
  5K = Resistor [tolerance=±5% resistance=4.7k package=THT]
  1N4148 = Rectifier Diode [part_number=1N4148 package="300 mil [THT]"]
  10K = Resistor [tolerance=±5% resistance=10k package=THT]
  DCC_Input = Screw terminal - 2 pins [package=THT]
  270pF = Ceramic Capacitor [capacitance=0.1nF package="200 mil [THT, multilayer]"]
  Arduino_Nano = Arduino Nano (Rev3.0)
  BR = bridge rectifier round [package="round [THT]"]
  L7805 = Voltage Regulator - 5V [package="TO220 [THT]"]
  470_uF = Electrolytic Capacitor [capacitance=1µF package="100 mil [THT, electrolytic]"]
  1_3K = Resistor [tolerance=±5% resistance=1.5k package=THT]
  0_1_uF = Ceramic Capacitor [capacitance=100nF voltage=50V package="200 mil [THT, multilayer]"]

nets:
  N1: 6N137.pin2, 1N4148.cathode, 270pF.0, 1_3K.Pin_1
  N2: 6N137.pin3, 1N4148.anode, DCC_Input.pin2, 270pF.1, BR.AC#0
  GND: 6N137.pin5, Arduino_Nano.GND, BR.DC-, L7805.GND, 470_uF.-, 0_1_uF.1
  N3: 6N137.pin6, 5K.Pin_1, Arduino_Nano.D2
  N4: 6N137.pin7, 10K.Pin_1
  N5: 6N137.pin8, 5K.Pin_0, 10K.Pin_0, Arduino_Nano.5V, L7805.output_voltage, 470_uF.+
  N6: DCC_Input.pin1, BR.AC#1, 1_3K.Pin_0
  N7: BR.DC+, L7805.input_voltage, 0_1_uF.0

notes:
  to DCC
  5V DC
  DCC Interface - http://www.mynabay.com/dcc_monitor/
  Bob Gamble
  D1/TX D0/RX RST GND  D2  D3*  D4  D5*  D6* D7  D8   D9* D10* D11* D12
  D13 3V3 REF A0  A1  A2  A3  A4  A5  A6 A7 5V RST GND VIN
  GRND
  Rev 1.1
  D12 D11* D10* D9*  D8  D7  D6*  D5*  D4 D3*  D2  GND RST D0/RX D1/TX
  VIN GND RST  5V A7  A6 A5  A4  A3  A2  A1  A0 REF 3V3 D13
  JMP TO GRND OR REF
  DCC Powered
  Rev 1.3
  +5v
  Nano Interface
  <- GRND
  <- +5v
